# Fritzing sketch client_engine_rpm_capture (saved by Fritzing 0.9.3b)
breadboards: 1

parts:
  R1 = Resistor [tolerance=±5% resistance=470 package="0402 [SMD]"]
  WeMos_D1_Mini1 = WeMos D1 Mini  # not connected
  R2 = Resistor [tolerance=±5% resistance=1k package="0402 [SMD]"]
  LED1 = smd LED [color="Red (633nm)" package="1206 [SMD]"]
  D1 = Zener Diode [part_number=1N4732A breakdown_voltage=5.1V package="Melf DO-213 AB [SMD]"]

nets:
  N1: R1.Pin_0, D1.anode
  N2: R2.Pin_0, D1.cathode
  N3: R2.Pin_1, LED1.cathode

notes:
  Arduino D1 mini
  470Ω
  轉速截取機 - CLIENT
  羽山秋人 https://3wa.tw
  2024-07-15
  3~5V
  GND
  轉速訊號輸入，可接：
  1. 碼表轉速訊號
  2. 晶式高壓線圈輸入端黑線或綠線
  3. 凸台脈衝號訊號
  PC817
  Zener 5.1V
  1KΩ
